# Fritzing sketch 01_Blink (saved by Fritzing 1.0.2b)
breadboards: 1

parts:
  U1 = LuaNode32 / ESP32 [part_number=ESP32S-PIN30]
  LED1 = LED - 5mm [color="Red (633nm)" current=0.030A package="5 mm [THT]"]

nets:
  N1: U1.GND, LED1.cathode
  N2: U1.D18, LED1.anode

custom parts:
  LuaNode32 / ESP32: New Image for LuaNode32 DOIT ESP32 DEVKIT V1. Base parts from LuaNode32 / ESP32 ESP32 based LuaNode32 by G.Noorlander DOIT Esp32 DevKit v1 (30 pins long, 11 pins width) by Werner Rothschopf (modified by vanepp Dec 2018)
