# Fritzing sketch 02_Button (saved by Fritzing 1.0.2b)
breadboards: 1

parts:
  U1 = LuaNode32 / ESP32 [part_number=ESP32S-PIN30]
  S1 = Pushbutton [package="[THT]"]

nets:
  N1: U1.GND, S1.Pin_3, S1.Pin_4
  N2: U1.D19, S1.Pin_1, S1.Pin_2

custom parts:
  LuaNode32 / ESP32: New Image for LuaNode32 DOIT ESP32 DEVKIT V1. Base parts from LuaNode32 / ESP32 ESP32 based LuaNode32 by G.Noorlander DOIT Esp32 DevKit v1 (30 pins long, 11 pins width) by Werner Rothschopf (modified by vanepp Dec 2018)
